# Fritzing sketch Esp8266-01_4RelayBoard (saved by Fritzing 0.9.3b)
breadboards: 1

parts:
  Reset = Pushbutton [package="[SMD]"]
  Factory_reset = Pushbutton [package="[SMD]"]
  U1 = V_REG_LD1117VXX [part_number=ASM117 package=78xxl]
  C2 = Electrolytic Capacitor [capacitance=47µF voltage=20V package="100 mil [THT, electrolytic]"]
  C3 = Electrolytic Capacitor [capacitance=47µF voltage=20V package="100 mil [THT, electrolytic]"]
  JP2 = Header 2 [part_number=220Vac package=screwterminal-3.5mm-2_lock]
  U2 = Module 4 Relais 5V [part_number="4RElay Module" package="Module 4 Relais 5V"]
  HLK-PM1 = HLK-PM01
  Fuse1 = Fuse with Handler [part_number=Htc-15m]
  Espessif_Serial_Wifi_Modul_1 = ESP8266 ESP01 [part_number=ESP8266 package=THT]

nets:
  N1: Reset.Pin_1, Reset.Pin_2, Espessif_Serial_Wifi_Modul_1.GPIO16
  GND: Reset.Pin_3, Reset.Pin_4, Factory_reset.Pin_3, Factory_reset.Pin_4, U1.GND, C2.-, C3.-, U2.GND, HLK-PM1.-Vo, Espessif_Serial_Wifi_Modul_1.GND
  N2: Factory_reset.Pin_1, Factory_reset.Pin_2, U2.IN3, Espessif_Serial_Wifi_Modul_1.RXD
  3.3V: U1.OUT, C2.+, Espessif_Serial_Wifi_Modul_1.VCC, Espessif_Serial_Wifi_Modul_1.CH_PD
  10V: U1.IN, C3.+, U2.VCC, Fuse1.Connector2
  N3: JP2.1, HLK-PM1.AC#1
  N4: JP2.2, HLK-PM1.AC#0
  N5: U2.IN1, Espessif_Serial_Wifi_Modul_1.GPIO00
  N6: U2.IN2, Espessif_Serial_Wifi_Modul_1.GPIO02
  N7: U2.IN4, Espessif_Serial_Wifi_Modul_1.TXD
  5V: U2.JD-VCC, U2.VCC2
  N8: HLK-PM1.+Vo, Fuse1.Connector1

notes:
  Reset
  Factory reset
  ESP8266-01
  ESP8266-01 OTA module, ESP8266-01 4 relay board, 1.0
  220AC
  5Vdc
  3.3Vdc

custom parts:
  Module 4 Relais 5V: Module 4 Relais 5V 4x SPD-06VDC-SD-C
  ESP8266 ESP01: Generic WiFi Module based on the ESP8266 with onboard PCB antenna and UART communications
