# Fritzing sketch Esp8266-01_4Outputfzz (saved by Fritzing 0.9.3b)
breadboards: 1

parts:
  Espessif_Serial_Wifi_Modul_1 = ESP8266 ESP01 [part_number=ESP8266 package=THT]
  Reset = Pushbutton [package="[SMD]"]
  Factory_reset = Pushbutton [package="[SMD]"]
  U1 = V_REG_LD1117VXX [part_number=ASM117 package=78xxl]
  C2 = Electrolytic Capacitor [capacitance=47µF voltage=20V package="100 mil [THT, electrolytic]"]
  C3 = Electrolytic Capacitor [capacitance=47µF voltage=20V package="100 mil [THT, electrolytic]"]
  JP2 = Header 2 [part_number=5Vdc package=screwterminal-3.5mm-2_lock]

nets:
  GND: Espessif_Serial_Wifi_Modul_1.GND, Reset.Pin_1, Reset.Pin_2, Factory_reset.Pin_3, Factory_reset.Pin_4, U1.GND, C2.-, C3.-, JP2.2
  GPIO3: Espessif_Serial_Wifi_Modul_1.RXD
  GPIO1: Espessif_Serial_Wifi_Modul_1.TXD, Factory_reset.Pin_1, Factory_reset.Pin_2
  3.3V: Espessif_Serial_Wifi_Modul_1.VCC, Espessif_Serial_Wifi_Modul_1.CH_PD, U1.OUT, C2.+
  N1: Espessif_Serial_Wifi_Modul_1.GPIO16, Reset.Pin_3, Reset.Pin_4
  GPIO0: Espessif_Serial_Wifi_Modul_1.GPIO00
  GPIO2: Espessif_Serial_Wifi_Modul_1.GPIO02
  N2: U1.IN, C3.+, JP2.1

notes:
  Reset
  Factory reset
  3.3V FTDI
  GPIO 0
  GPIO 2
  ESP8266-01
  5Vdc
  ESP8266-01 OTA module, ESP8266-01 4 output, 1.0
  GPIO1
  GPIO3

custom parts:
  ESP8266 ESP01: Generic WiFi Module based on the ESP8266 with onboard PCB antenna and UART communications
